# Fritzing sketch fritzing_schematic_thesis (saved by Fritzing 1.0.7)

parts:
  A1 = Raspberry Pi Pico2
  A2 = DFR0379
  U1 = IC, SIP package, 4 pins [chip_label=LiDAR]
  JACK1 = 2.1mm DC Barrel Jack
  DRV_1 = DRV 8825 Stepper Motor Carrier, High Current [part_number="DRV 8825"]
  M2 = Stepper Motor - Bipolar
  C1 = Capacitor Polarized [package=panasonic_d]
  Mod1 = KY-024 Linear Hall Magnetic Sensor Module [package="Breakout board"]

nets:
  N1: A1.pin_2, U1.pin1
  N2: A1.pin_3, A1.pin_13, A1.pin_18, A1.pin_33, A1.pin_38, A2.Pin_3, A2.Pin_6, U1.pin3, JACK1.sleeve, DRV_1.GROUND_ST/_MT, C1.-, Mod1.G, Mod1.D0
  N3: A1.pin_19, DRV_1.STEP
  N4: A1.pin_20, DRV_1.DIRECTION
  N5: A1.pin_36, Mod1.+
  N6: A1.pin_39, A1.pin_40, A2.Pin_7, A2.Pin_8, U1.pin4, DRV_1.SLEEP
  N7: A2.Pin_1, A2.Pin_2, JACK1.center, DRV_1.VOLTAGE_ST/_MT, C1.+
  N8: DRV_1.OUT_2B, M2.A
  N9: DRV_1.OUT_2A, M2.C
  N10: DRV_1.OUT_1A, M2.B
  N11: DRV_1.OUT_1B, M2.D

notes:
  Tx
  GND
  5V
  PWM
  12V
  100 μF
  3.3V

custom parts:
  Raspberry Pi Pico2: Raspberry Pi Pico 2W is our new $7 microcontroller board, built on RP2350: our new high-performance, secure microcontroller with on board WiFi.
  DFR0379: 20W Adjustable DC-DC Buck Converter with Digital Display.
  KY-024 Linear Hall Magnetic Sensor Module: KY-024 Linear Hall Magnetic Sensor Module reacts iin the presence of a magnetic field.
